# Fritzing sketch legion Mark 2 Circuit Diagram (saved by Fritzing 0.9.3b)

parts:
  Part1 = 16-Channel 12-bit PWM Servo Driver - I2C [part_number=815]
  SERVO1 = Tower Pro SG90 servo [part_number=101246]
  S1 = H-Bridge with L298N
  Part2 = Arduino Nano (Rev3.0) (ICSP)
  U1 = LM2596 step down module
  BAT1 = 18650 battery holder [package=battery-18650-kit]
  Mod1 = ESP32 - CAM
  M1 = DC Mini Metal Gear Motor
  M3 = DC Mini Metal Gear Motor
  M5 = DC Mini Metal Gear Motor
  M6 = DC Mini Metal Gear Motor
  SERVO2 = Tower Pro SG90 servo [part_number=101246]
  SERVO3 = Tower Pro SG90 servo [part_number=101246]
  SERVO4 = Tower Pro SG90 servo [part_number=101246]
  SERVO5 = Tower Pro SG90 servo [part_number=101246]
  SERVO6 = Tower Pro SG90 servo [part_number=101246]
  SERVO7 = Tower Pro SG90 servo [part_number=101246]
  SERVO8 = Tower Pro SG90 servo [part_number=101246]
  SERVO9 = Tower Pro SG90 servo [part_number=101246]
  SERVO10 = Tower Pro SG90 servo [part_number=101246]
  SERVO11 = Tower Pro SG90 servo [part_number=101246]
  SERVO12 = Tower Pro SG90 servo [part_number=101246]
  BAT2 = 18650 battery holder [package=battery-18650-kit]
  BAT3 = 18650 battery holder [package=battery-18650-kit]

nets:
  N1: Part1.PWRIN, U1.OUT+, Mod1.5V
  GND: Part1.GND, S1.12V, S1.GND, Part2.GND, U1.IN+, U1.IN-, U1.OUT-, BAT1.-, Mod1.GND, BAT2.+
  N2: Part1.PWM6, SERVO2.Signal
  N3: Part1.PWM5, SERVO1.Signal
  N4: Part1.PWM4, SERVO9.Signal
  N5: Part1.PWM2, SERVO10.Signal
  N6: Part1.PWM1, SERVO11.Signal
  N7: Part1.PWM0, SERVO12.Signal
  VCC: Part1.VCC, Part2.3V3
  N8: Part1.SDA, Part2.A4
  N9: Part1.SCL, Part2.A5
  N10: Part1.PWM14, SERVO6.Signal
  N11: Part1.PWM13, SERVO7.Signal
  N12: Part1.PWM12, SERVO8.Signal
  N13: Part1.PWM10, SERVO5.Signal
  N14: Part1.PWM9, SERVO3.Signal
  N15: Part1.PWM8, SERVO4.Signal
  5V: S1.5V, Part2.5V
  N16: S1.ENA, Part2.D6, Part2.D7
  N17: S1.IN1, Part2.D2
  N18: S1.IN2, Part2.D3
  N19: S1.IN3, Part2.D4
  N20: S1.IN4, Part2.D5
  N21: S1.ENB, Part2.D9, Part2.D10
  N22: S1.M1-01, M5.IN2, M6.IN2
  N23: S1.M1-02, M5.IN1, M6.IN1
  N24: S1.M2-01, M1.IN2, M3.IN2
  N25: S1.M2-02, M1.IN1, M3.IN1
  N26: Part2.D1/TX, Mod1.VOR
  N27: Part2.D0/RX, Mod1.VOT
  N28: BAT1.+, BAT3.-
  N29: BAT2.-, BAT3.+

custom parts:
  16-Channel 12-bit PWM Servo Driver - I2C: You want to make a cool robot, maybe a hexapod walker, or maybe just a piece of art with a lot of moving parts. Or maybe you want to drive a lot of LEDs with precise PWM output. Using only two pins, control 16 free-running PWM outputs! You can even chain up 62 breakouts to control up to 992 PWM outputs.
  Tower Pro SG90 servo: Original file by John De Cristofaro http://www.adafruit.com/products/1449 Adafruit Feedback Servo (Small) Edited by: e-radionica.com 28/9/2015
  H-Bridge with L298N: h-bridge
  LM2596 step down module: LM2596 DC-DC step down power supply module 3 A.
  18650 battery holder: 18650 Battery Holder
  ESP32 - CAM: The ESP32-CAM has a very competitive small-size camera module that can operate independently as a minimum system with a footprint of only 27*40.5*4.5mm and a deep sleep current of up to 6mA.
